// Logisim project ALU.circ as structural Verilog
module Half_Adder_1_bit (
  input  A,
  input  B,
  output S,
  output C
);

  xor xor_1 (S, A, B);
  and and_1 (C, A, B);
endmodule

module Full_Adder_1_bit (
  input  A,
  input  B,
  input  Ci,
  output S,
  output Co
);

  wire HA1_c, HA1_s, HA2_c;

  Half_Adder_1_bit HA1 (.A(A), .B(B), .S(HA1_s), .C(HA1_c));
  Half_Adder_1_bit HA2 (.A(HA1_s), .B(Ci), .S(S), .C(HA2_c));
  or or_1 (Co, HA2_c, HA1_c);
endmodule

module MUX_2_1 (
  input  A,
  input  B,
  input  S0,
  output OUT
);

  wire and_1_out, and_2_out;

  and and_1 (and_1_out, A, ~S0);  // AND_Gate
  and and_2 (and_2_out, B, S0);
  or or_1 (OUT, and_1_out, and_2_out);
endmodule

// ADD
module Subtractor_1_bit (
  input  A,
  input  B,
  input  nB,
  input  Ci,
  output S0,
  output Co
);

  wire xor_1_out;

  xor xor_1 (xor_1_out, B, nB);
  Full_Adder_1_bit FA (.A(A), .B(xor_1_out), .Ci(Ci), .S(S0), .Co(Co));
endmodule

module Full_Adder_4_bit (
  input  Ci,
  input  [3:0] X,
  input  [3:0] Y,
  output [3:0] Z,
  output Co
);

  wire FA1b_2_co, FA1b_3_co, FA1b_co;

  Full_Adder_1_bit FA1b (.A(X[0]), .B(Y[0]), .Ci(Ci), .S(Z[0]), .Co(FA1b_co));
  Full_Adder_1_bit FA1b_2 (.A(X[1]), .B(Y[1]), .Ci(FA1b_co), .S(Z[1]), .Co(FA1b_2_co));
  Full_Adder_1_bit FA1b_3 (.A(X[2]), .B(Y[2]), .Ci(FA1b_2_co), .S(Z[2]), .Co(FA1b_3_co));
  Full_Adder_1_bit FA1b_4 (.A(X[3]), .B(Y[3]), .Ci(FA1b_3_co), .S(Z[3]), .Co(Co));
endmodule

module MUX_3_1 (
  input  A,
  input  B,
  input  C,
  input  S0,
  input  S1,
  output OUT
);

  wire and_1_out, and_2_out, and_3_out;

  and and_1 (and_1_out, A, ~S0, ~S1);  // AND_Gate
  and and_2 (and_2_out, B, ~S0, S1);  // AND_Gate
  and and_3 (and_3_out, C, S0, ~S1);  // AND_Gate
  or or_1 (OUT, and_1_out, and_2_out, and_3_out);
endmodule

// ALU
module ALU_1_bit (
  input  A,
  input  B,
  input  Nb,
  input  Ci,
  input  [1:0] Op,
  output Z,
  output Over,
  output Co
);

  wire and_1_out, mux_2_1_1_out, or_1_out, subtractor_1_bit_1_s0;

  Subtractor_1_bit subtractor_1_bit_1 (.A(A), .B(B), .nB(Nb), .S0(subtractor_1_bit_1_s0), .Ci(Ci), .Co(Co));
  and and_1 (and_1_out, A, B);
  or or_1 (or_1_out, A, B);
  MUX_2_1 mux_2_1_1 (.A(and_1_out), .B(or_1_out), .S0(Op[0]), .OUT(mux_2_1_1_out));
  MUX_2_1 mux_2_1_2 (.A(mux_2_1_1_out), .B(subtractor_1_bit_1_s0), .S0(Op[1]), .OUT(Z));
  xor xor_1 (Over, Co, Ci);

  // Notes on the sheet:
  //   AND / OR
  //   Logic / Math
endmodule

module Subtractor_4_bit (
  input  [3:0] A,
  input  [3:0] B,
  input  Ci,
  output [3:0] S,
  output Co
);

  wire subtractor_1_bit_1_co, subtractor_1_bit_2_co, subtractor_1_bit_3_co;

  Subtractor_1_bit subtractor_1_bit_1 (.A(A[0]), .B(B[0]), .nB(Ci), .S0(S[0]), .Ci(Ci), .Co(subtractor_1_bit_1_co));
  Subtractor_1_bit subtractor_1_bit_2 (
    .A(A[1]), .B(B[1]), .nB(Ci), .S0(S[1]), .Ci(subtractor_1_bit_1_co), .Co(subtractor_1_bit_2_co));
  Subtractor_1_bit subtractor_1_bit_3 (
    .A(A[2]), .B(B[2]), .nB(Ci), .S0(S[2]), .Ci(subtractor_1_bit_2_co), .Co(subtractor_1_bit_3_co));
  Subtractor_1_bit subtractor_1_bit_4 (.A(A[3]), .B(B[3]), .nB(Ci), .S0(S[3]), .Ci(subtractor_1_bit_3_co), .Co(Co));
endmodule

module ALU_8_bit (
  input  [1:0] Op,
  input  [7:0] A,
  input  [7:0] B,
  output [7:0] S,
  output Zero,
  output Neg,
  output Over,
  output Co
);

  wire alu_1_bit_1_co, alu_1_bit_2_co, alu_1_bit_3_co, alu_1_bit_4_co, alu_1_bit_5_co, alu_1_bit_6_co,
       alu_1_bit_7_co, and_1_out;

  and and_1 (and_1_out, Op[0], Op[1]);
  ALU_1_bit alu_1_bit_1 (
    .A(A[0]), .B(B[0]), .Nb(and_1_out), .Ci(and_1_out), .Op(Op), .Z(S[0]), .Co(alu_1_bit_1_co));  // open: Over
  ALU_1_bit alu_1_bit_2 (
    .A(A[1]), .B(B[1]), .Nb(and_1_out), .Ci(alu_1_bit_1_co), .Op(Op), .Z(S[1]), .Co(alu_1_bit_2_co));  // open: Over
  ALU_1_bit alu_1_bit_3 (
    .A(A[2]), .B(B[2]), .Nb(and_1_out), .Ci(alu_1_bit_2_co), .Op(Op), .Z(S[2]), .Co(alu_1_bit_3_co));  // open: Over
  ALU_1_bit alu_1_bit_4 (
    .A(A[3]), .B(B[3]), .Nb(and_1_out), .Ci(alu_1_bit_3_co), .Op(Op), .Z(S[3]), .Co(alu_1_bit_4_co));  // open: Over
  ALU_1_bit alu_1_bit_5 (
    .A(A[4]), .B(B[4]), .Nb(and_1_out), .Ci(alu_1_bit_4_co), .Op(Op), .Z(S[4]), .Co(alu_1_bit_5_co));  // open: Over
  ALU_1_bit alu_1_bit_6 (
    .A(A[5]), .B(B[5]), .Nb(and_1_out), .Ci(alu_1_bit_5_co), .Op(Op), .Z(S[5]), .Co(alu_1_bit_6_co));  // open: Over
  ALU_1_bit alu_1_bit_7 (
    .A(A[6]), .B(B[6]), .Nb(and_1_out), .Ci(alu_1_bit_6_co), .Op(Op), .Z(S[6]), .Co(alu_1_bit_7_co));  // open: Over
  ALU_1_bit alu_1_bit_8 (
    .A(A[7]), .B(B[7]), .Nb(and_1_out), .Ci(alu_1_bit_7_co), .Op(Op), .Z(Neg), .Over(Over), .Co(Co));
  nor nor_1 (Zero, S[0], S[1], S[2], S[3], S[4], S[5], S[6], Neg);

  assign S[7] = Neg;
endmodule

module Full_Adder_8_bit (
  input  [7:0] X,
  input  [7:0] Y,
  input  Ci,
  output [7:0] Z
);

  wire full_adder_4_bit_1_co;

  Full_Adder_4_bit full_adder_4_bit_1 (.Ci(Ci), .X(Y[3:0]), .Y(X[3:0]), .Z(Z[3:0]), .Co(full_adder_4_bit_1_co));
  Full_Adder_4_bit full_adder_4_bit_2 (.Ci(full_adder_4_bit_1_co), .X(Y[7:4]), .Y(X[7:4]), .Z(Z[7:4]));  // open: Co
endmodule
