// Logisim project REG.circ as structural Verilog
// SR
module BistabileSR (
  input  R,
  input  Reset,
  input  S,
  output Q,
  output negQ
);

  nand nand_1 (Q, R, negQ);
  nand nand_2 (negQ, Q, Reset, S);
endmodule

// SR
module LatchSR (
  input  S,
  input  Clock,
  input  R,
  input  Reset,
  output Q,
  output negQ
);

  wire nand_1_out, nand_2_out;

  nand nand_1 (nand_1_out, S, Clock);
  nand nand_2 (nand_2_out, Clock, R);
  BistabileSR bistabilesr_1 (.R(nand_1_out), .Reset(Reset), .S(nand_2_out), .Q(Q), .negQ(negQ));
endmodule

// LD
module LatchD (
  input  D,
  input  Clock,
  input  Reset,
  output Q,
  output negQ
);

  wire not_1_out;

  not not_1 (not_1_out, D);
  LatchSR LatchSR (.S(D), .Clock(Clock), .R(not_1_out), .Reset(Reset), .Q(Q), .negQ(negQ));
endmodule

module FFD (
  input  D,
  input  En,
  input  Clock,
  input  Reset,
  output Q
);

  wire latchd_1_q, mux2_1_1_out, not_1_out;

  MUX2_1 mux2_1_1 (.A(Q), .B(D), .S0(En), .OUT(mux2_1_1_out));
  not not_1 (not_1_out, Clock);
  LatchD latchd_1 (.D(mux2_1_1_out), .Clock(not_1_out), .Reset(Reset), .Q(latchd_1_q));  // open: negQ
  LatchD latchd_2 (.D(latchd_1_q), .Clock(Clock), .Reset(Reset), .Q(Q));  // open: negQ
endmodule

// MX
module MUX2_1 (
  input  A,
  input  B,
  input  S0,
  output OUT
);

  wire and_1_out, and_2_out;

  and and_1 (and_1_out, A, ~S0);  // AND_Gate
  and and_2 (and_2_out, B, S0);
  or or_1 (OUT, and_1_out, and_2_out);
endmodule

module Reg8b (
  input  [7:0] D,
  input  EN,
  input  CLK,
  input  Reset_n,
  output [7:0] Q
);

  FFD ffd_1 (.D(D[0]), .En(EN), .Clock(CLK), .Reset(Reset_n), .Q(Q[0]));
  FFD ffd_2 (.D(D[1]), .En(EN), .Clock(CLK), .Reset(Reset_n), .Q(Q[1]));
  FFD ffd_3 (.D(D[2]), .En(EN), .Clock(CLK), .Reset(Reset_n), .Q(Q[2]));
  FFD ffd_4 (.D(D[3]), .En(EN), .Clock(CLK), .Reset(Reset_n), .Q(Q[3]));
  FFD ffd_5 (.D(D[4]), .En(EN), .Clock(CLK), .Reset(Reset_n), .Q(Q[4]));
  FFD ffd_6 (.D(D[5]), .En(EN), .Clock(CLK), .Reset(Reset_n), .Q(Q[5]));
  FFD ffd_7 (.D(D[6]), .En(EN), .Clock(CLK), .Reset(Reset_n), .Q(Q[6]));
  FFD ffd_8 (.D(D[7]), .En(EN), .Clock(CLK), .Reset(Reset_n), .Q(Q[7]));
endmodule

module RegFile (
  input  Dmsel,
  input  [1:0] Areg,
  input  [1:0] Sel,
  input  [1:0] Breg,
  input  CLK,
  input  Reset_n,
  input  [7:0] Data,
  output [7:0] _3,
  output [7:0] _2,
  output [7:0] _1,
  output [7:0] _0,
  output [7:0] Aval,
  output [7:0] Bval
);

  wire demultiplexer_1_out0, demultiplexer_1_out1, demultiplexer_1_out2, demultiplexer_1_out3;

  Demultiplexer #(.select(2)) demultiplexer_1 (
    .out0(demultiplexer_1_out0), .out1(demultiplexer_1_out1), .out2(demultiplexer_1_out2),
    .out3(demultiplexer_1_out3), .in(Dmsel), .sel(Sel));  // open: en
  Reg8b R0 (.EN(demultiplexer_1_out0), .CLK(CLK), .D(Data), .Q(_0), .Reset_n(Reset_n));
  Reg8b R1 (.EN(demultiplexer_1_out1), .CLK(CLK), .D(Data), .Q(_1), .Reset_n(Reset_n));
  Reg8b R2 (.EN(demultiplexer_1_out2), .CLK(CLK), .D(Data), .Q(_2), .Reset_n(Reset_n));
  Reg8b R3 (.EN(demultiplexer_1_out3), .CLK(CLK), .D(Data), .Q(_3), .Reset_n(Reset_n));
  Multiplexer #(.select(2), .width(8)) multiplexer_1 (
    .in0(_0), .in1(_1), .in2(_2), .in3(_3), .out(Aval), .sel(Areg));  // open: en
  Multiplexer #(.select(2), .width(8)) multiplexer_2 (
    .in0(_0), .in1(_1), .in2(_2), .in3(_3), .out(Bval), .sel(Breg));  // open: en
endmodule
