// Logisim project datapath.circ as structural Verilog: 3 circuits, main circuit main
module main (
  input  Reset,
  output [7:0] R0,
  output [7:0] R1,
  output [7:0] R2,
  output [7:0] R3
);

  wire alu_8_bit_1_zero, and_1_out, clock_1_out, control_unit_1_alusrc, control_unit_1_branch,
       control_unit_1_mem2reg, control_unit_1_memread, control_unit_1_memwrite, control_unit_1_regwrite,
       not_1_out, not_2_out;
  wire [1:0] alucontrol_1_aluctrl, control_unit_1_opcode, control_unit_1_rd, control_unit_1_rs1,
       control_unit_1_rs2;
  wire [7:0] alu_8_bit_1_s, control_unit_1_immediate, full_adder_8_bit_1_z, full_adder_8_bit_2_z,
       multiplexer_1_out, multiplexer_2_out, multiplexer_3_out, ram_2_data, reg8b_1_q, regfile_1_aval,
       regfile_1_bval;
  wire [15:0] ram_1_data;

  Multiplexer #(.width(8)) multiplexer_1 (
    .in0(full_adder_8_bit_1_z), .in1(full_adder_8_bit_2_z), .out(multiplexer_1_out), .sel(and_1_out));  // open: en
  Clock clock_1 (.out(clock_1_out));
  Full_Adder_8_bit full_adder_8_bit_1 (
    .Ci(1'b0), .X(reg8b_1_q), .Y(control_unit_1_immediate), .Z(full_adder_8_bit_1_z));
  Reg8b reg8b_1 (.EN(1'b1), .CLK(clock_1_out), .D(multiplexer_1_out), .Q(reg8b_1_q), .Reset_n(Reset));
  Full_Adder_8_bit full_adder_8_bit_2 (.Ci(1'b0), .X(reg8b_1_q), .Y(8'h1), .Z(full_adder_8_bit_2_z));
  and and_1 (and_1_out, control_unit_1_branch, alu_8_bit_1_zero);
  RAM #(.dataWidth(16), .bus("separate")) ram_1 (
    .addr(reg8b_1_q), .data(ram_1_data), .str(1'b0), .clk(clock_1_out), .ld(1'b1), .clr(not_1_out));  // open: din, sel
  not not_1 (not_1_out, Reset);
  Control_Unit control_unit_1 (
    .Istr(ram_1_data), .Immediate(control_unit_1_immediate), .ALUSrc(control_unit_1_alusrc),
    .MEM2Reg(control_unit_1_mem2reg), .RegWrite(control_unit_1_regwrite), .MEMRead(control_unit_1_memread),
    .MEMWrite(control_unit_1_memwrite), .branch(control_unit_1_branch), .RS2(control_unit_1_rs2),
    .RS1(control_unit_1_rs1), .RD(control_unit_1_rd), .Opcode(control_unit_1_opcode));
  RegFile regfile_1 (
    .Data(multiplexer_3_out), .Dmsel(control_unit_1_regwrite), .Sel(control_unit_1_rd),
    .Aval(regfile_1_aval), .Bval(regfile_1_bval), .Areg(control_unit_1_rs2), .Breg(control_unit_1_rs1),
    .CLK(clock_1_out), ._0(R0), ._1(R1), ._2(R2), ._3(R3), .Reset_n(Reset));
  Multiplexer #(.width(8)) multiplexer_2 (
    .in0(regfile_1_bval), .in1(control_unit_1_immediate), .out(multiplexer_2_out), .sel(control_unit_1_alusrc));  // open: en
  ALUControl alucontrol_1 (.in_1(control_unit_1_opcode), .Istr(ram_1_data), .ALUCtrl(alucontrol_1_aluctrl));
  ALU_8_bit alu_8_bit_1 (
    .Zero(alu_8_bit_1_zero), .Op(alucontrol_1_aluctrl), .A(regfile_1_aval), .B(multiplexer_2_out),
    .S(alu_8_bit_1_s));  // open: Neg, Over, Co
  not not_2 (not_2_out, Reset);
  RAM #(.bus("separate")) ram_2 (
    .addr(alu_8_bit_1_s), .din(regfile_1_bval), .data(ram_2_data), .str(control_unit_1_memwrite),
    .clk(clock_1_out), .ld(control_unit_1_memread), .clr(not_2_out));  // open: sel
  Multiplexer #(.width(8)) multiplexer_3 (
    .in0(alu_8_bit_1_s), .in1(ram_2_data), .out(multiplexer_3_out), .sel(control_unit_1_mem2reg));  // open: en

  // Other names for the same wires on the sheet: R[31:0] = {R3, R2, R1, R0}
endmodule

module Control_Unit (
  input  [15:0] Istr,
  output [7:0] Immediate,
  output ALUSrc,
  output MEM2Reg,
  output RegWrite,
  output MEMRead,
  output [1:0] RS2,
  output [1:0] RS1,
  output [1:0] RD,
  output MEMWrite,
  output branch,
  output [1:0] Opcode
);

  wire multiplexer_1_out, multiplexer_2_out;

  Multiplexer multiplexer_1 (.in0(1'b1), .in1(1'b0), .out(multiplexer_1_out), .sel(Istr[4]));  // open: en
  Multiplexer multiplexer_2 (.in0(1'b1), .in1(1'b0), .out(multiplexer_2_out), .sel(Istr[4]));  // open: en
  Multiplexer #(.select(2)) multiplexer_3 (
    .in0(1'b1), .in1(1'b0), .in2(1'b0), .in3(1'b1), .out(ALUSrc), .sel(Istr[1:0]));  // open: en
  Multiplexer #(.select(2)) multiplexer_4 (
    .in0(multiplexer_1_out), .in1(1'b0), .in2(1'b0), .in3(1'b0), .out(MEM2Reg), .sel(Istr[1:0]));  // open: en
  Multiplexer #(.select(2)) multiplexer_5 (
    .in0(1'b1), .in1(1'b0), .in2(1'b1), .in3(1'b0), .out(RegWrite), .sel(Istr[1:0]));  // open: en
  Multiplexer #(.select(2)) multiplexer_6 (
    .in0(multiplexer_2_out), .in1(1'b0), .in2(1'b0), .in3(1'b0), .out(MEMRead), .sel(Istr[1:0]));  // open: en
  Multiplexer #(.select(2)) multiplexer_7 (
    .in0(1'b0), .in1(1'b0), .in2(1'b0), .in3(1'b1), .out(MEMWrite), .sel(Istr[1:0]));  // open: en
  Multiplexer #(.select(2)) multiplexer_8 (
    .in0(1'b0), .in1(1'b1), .in2(1'b0), .in3(1'b0), .out(branch), .sel(Istr[1:0]));  // open: en
  Multiplexer #(.select(2), .width(8)) multiplexer_9 (
    .in0(Istr[15:8]), .in1({Istr[14], Istr[2], Istr[13:10], Istr[3], Istr[15]}), .in2({8{1'b0}}),
    .in3({Istr[15:10], Istr[3:2]}), .out(Immediate), .sel(Istr[1:0]));  // open: en

  assign Opcode = Istr[1:0];
  assign RD = Istr[3:2];
  assign RS1 = Istr[7:6];
  assign RS2 = Istr[9:8];
endmodule

module ALUControl (
  input  [1:0] in_1,
  input  [15:0] Istr,
  output [1:0] ALUCtrl
);

  wire [1:0] multiplexer_1_out;

  Multiplexer #(.select(3), .width(2)) multiplexer_1 (
    .in0(2'b10), .in2(2'b11), .in3(2'b00), .in4(2'b01), .out(multiplexer_1_out), .sel({Istr[10], Istr[5:4]}));  // open: in1, in5, in6, in7, en
  Multiplexer #(.select(2), .width(2)) multiplexer_2 (
    .in0(2'b10), .in1(2'b11), .in2(multiplexer_1_out), .in3(2'b10), .out(ALUCtrl), .sel(in_1));  // open: en

  // Notes on the sheet:
  //   00 = I-type
  //   01 = SB-Type
  //   11 = S-Type
  //   10 = R-Type
  //   01
  //   00
  //   10
  //   11
  //   Questo mi gestisce la categoria di istruzioni su cui voglio andare a lavorare
endmodule
